// Logisim project 12-bit Custom RISC-V Microprocessor_group_2.circ as structural Verilog: 5 circuits, main circuit Main
module Register_File (
  input  clk,
  input  [31:0] Write_Data,
  input  Enable,
  input  [2:0] Read_Reg_1,
  input  [2:0] Write_Register,
  input  [2:0] Read_Reg_2,
  output [31:0] Read_Data,
  output [31:0] Read_Data_2
);

  wire and_1_out, and_2_out, and_3_out, and_4_out, and_5_out, and_6_out, and_7_out, and_8_out,
       decoder_1_out0, decoder_1_out1, decoder_1_out2, decoder_1_out3, decoder_1_out4, decoder_1_out5,
       decoder_1_out6, decoder_1_out7;
  wire [31:0] R0_q, R1_q, R2_q, R3_q, R4_q, R5_q, R6_q, R7_q;

  Decoder #(.select(3), .enable("false")) decoder_1 (
    .out0(decoder_1_out0), .out1(decoder_1_out1), .out2(decoder_1_out2), .out3(decoder_1_out3),
    .out4(decoder_1_out4), .out5(decoder_1_out5), .out6(decoder_1_out6), .out7(decoder_1_out7),
    .sel(Write_Register));
  and and_1 (and_1_out, decoder_1_out0, Enable);
  and and_2 (and_2_out, decoder_1_out1, Enable);
  and and_3 (and_3_out, decoder_1_out2, Enable);
  and and_4 (and_4_out, decoder_1_out3, Enable);
  and and_5 (and_5_out, decoder_1_out4, Enable);
  and and_6 (and_6_out, decoder_1_out5, Enable);
  and and_7 (and_7_out, decoder_1_out6, Enable);
  and and_8 (and_8_out, decoder_1_out7, Enable);
  Register #(.width(32)) R0 (.D(Write_Data), .en(and_1_out), .Q(R0_q), .clk(clk));  // open: clr
  Register #(.width(32)) R1 (.D(Write_Data), .en(and_2_out), .Q(R1_q), .clk(clk));  // open: clr
  Register #(.width(32)) R2 (.D(Write_Data), .en(and_3_out), .Q(R2_q), .clk(clk));  // open: clr
  Register #(.width(32)) R3 (.D(Write_Data), .en(and_4_out), .Q(R3_q), .clk(clk));  // open: clr
  Register #(.width(32)) R4 (.D(Write_Data), .en(and_5_out), .Q(R4_q), .clk(clk));  // open: clr
  Register #(.width(32)) R5 (.D(Write_Data), .en(and_6_out), .Q(R5_q), .clk(clk));  // open: clr
  Register #(.width(32)) R6 (.D(Write_Data), .en(and_7_out), .Q(R6_q), .clk(clk));  // open: clr
  Register #(.width(32)) R7 (.D(Write_Data), .en(and_8_out), .Q(R7_q), .clk(clk));  // open: clr
  Multiplexer #(.select(3), .width(32), .enable("false")) multiplexer_1 (
    .in0(R0_q), .in1(R1_q), .in2(R2_q), .in3(R3_q), .in4(R4_q), .in5(R5_q), .in6(R6_q), .in7(R7_q),
    .out(Read_Data), .sel(Read_Reg_1));
  Multiplexer #(.select(3), .width(32), .enable("false")) multiplexer_2 (
    .in0(R0_q), .in1(R1_q), .in2(R2_q), .in3(R3_q), .in4(R4_q), .in5(R5_q), .in6(R6_q), .in7(R7_q),
    .out(Read_Data_2), .sel(Read_Reg_2));
endmodule

module Main (
  output [31:0] out_1,
  output [31:0] out_2,
  output [31:0] out_3,
  output [2:0] out_4,
  output [31:0] out_5,
  output out_6
);

  wire and_1_out, button_1_out, button_2_out, button_3_out, control_unit_1_alusrc, control_unit_1_binv,
       control_unit_1_branch, control_unit_1_cin, control_unit_1_memread, control_unit_1_memtoreg,
       control_unit_1_memwrite, control_unit_1_regdst, control_unit_1_writereg, project_alu_1_zero;
  wire [1:0] control_unit_1_aluop;
  wire [2:0] multiplexer_1_out;
  wire [8:0] rom_1_data;
  wire [15:0] adder_1_out, adder_2_out, bit_extender_2_out, bit_extender_3_out, multiplexer_3_out,
       register_1_q;
  wire [31:0] bit_extender_1_out, multiplexer_4_out, ram_1_data;

  Button button_1 (.out(button_1_out));
  Button button_2 (.out(button_2_out));
  Register #(.width(16)) register_1 (
    .D(multiplexer_3_out), .Q(register_1_q), .clk(button_1_out), .clr(button_2_out));  // open: en
  ROM #(.addrWidth(16), .dataWidth(12)) rom_1 (.addr(register_1_q), .data({out_4, rom_1_data}));  // open: sel
  Control_Unit control_unit_1 (
    .in_1(out_4), .ALUop(control_unit_1_aluop), .WriteReg(control_unit_1_writereg),
    .Binv(control_unit_1_binv), .Cin(control_unit_1_cin), .MemRead(control_unit_1_memread),
    .MemWrite(control_unit_1_memwrite), .Branch(control_unit_1_branch), .ALUsrc(control_unit_1_alusrc),
    .MemToReg(control_unit_1_memtoreg), .RegDst(control_unit_1_regdst));
  Multiplexer #(.width(3), .enable("false")) multiplexer_1 (
    .in0(rom_1_data[2:0]), .in1(rom_1_data[5:3]), .out(multiplexer_1_out), .sel(control_unit_1_regdst));
  assign bit_extender_1_out = {{29{1'b0}}, rom_1_data[2:0]};  // Bit_Extender bit_extender_1
  Register_File register_file_1 (
    .clk(button_1_out), .Write_Data(multiplexer_4_out), .Read_Data(out_1), .Enable(control_unit_1_writereg),
    .Read_Reg_1(rom_1_data[8:6]), .Read_Data_2(out_5), .Write_Register(multiplexer_1_out),
    .Read_Reg_2(rom_1_data[5:3]));
  Multiplexer #(.width(32), .enable("false")) multiplexer_2 (
    .in0(out_5), .in1(bit_extender_1_out), .out(out_2), .sel(control_unit_1_alusrc));
  Adder #(.width(16)) adder_1 (.a(16'h1), .b(register_1_q), .out(adder_1_out));  // open: cin, cout
  Bit_Extender #(.in_width(32)) bit_extender_2 (.in(bit_extender_1_out), .out(bit_extender_2_out));
  Project_ALU project_alu_1 (
    .Cin(control_unit_1_cin), .Cout(out_6), .Binv(control_unit_1_binv), .ALUop(control_unit_1_aluop),
    .S(out_3), .Zero(project_alu_1_zero), .A(out_1), .B(out_2));
  Adder #(.width(16)) adder_2 (.a(adder_1_out), .b(bit_extender_2_out), .out(adder_2_out));  // open: cin, cout
  and and_1 (and_1_out, project_alu_1_zero, control_unit_1_branch);
  Multiplexer #(.width(16), .enable("false")) multiplexer_3 (
    .in0(adder_1_out), .in1(adder_2_out), .out(multiplexer_3_out), .sel(and_1_out));
  Bit_Extender #(.in_width(32)) bit_extender_3 (.in(out_3), .out(bit_extender_3_out));
  RAM #(.addrWidth(16), .dataWidth(32), .bus("separate")) ram_1 (
    .addr(bit_extender_3_out), .din(out_5), .data(ram_1_data), .str(control_unit_1_memwrite),
    .clk(button_1_out), .ld(control_unit_1_memread), .clr(button_3_out));  // open: sel
  Multiplexer #(.width(32), .enable("false")) multiplexer_4 (
    .in0(out_3), .in1(ram_1_data), .out(multiplexer_4_out), .sel(control_unit_1_memtoreg));
  Button button_3 (.out(button_3_out));
endmodule

module _1_bit_ALU (
  input  Cin,
  input  A,
  input  B,
  input  [1:0] ALUop,
  input  Binv,
  output S,
  output Cout
);

  wire adder_1_out, and_1_out, multiplexer_1_out, not_1_out, or_1_out;

  not not_1 (not_1_out, B);
  and and_1 (and_1_out, A, B);
  or or_1 (or_1_out, A, B);
  Multiplexer multiplexer_1 (.in0(B), .in1(not_1_out), .out(multiplexer_1_out), .sel(Binv));  // open: en
  Adder #(.width(1)) adder_1 (.a(A), .b(multiplexer_1_out), .out(adder_1_out), .cin(Cin), .cout(Cout));
  Multiplexer #(.select(2)) multiplexer_2 (
    .in0(and_1_out), .in1(or_1_out), .in2(adder_1_out), .out(S), .sel(ALUop));  // open: in3, en
endmodule

module Project_ALU (
  input  Cin,
  input  [31:0] A,
  input  [31:0] B,
  input  Binv,
  input  [1:0] ALUop,
  output Cout,
  output [31:0] S,
  output Zero
);

  wire comparator_1_lt;
  wire [31:0] adder_1_out, bit_extender_1_out, multiplexer_1_out, not_1_out;

  assign not_1_out = ~B;  // NOT_Gate not_1, 32 bits wide
  Multiplexer #(.width(32), .enable("false")) multiplexer_1 (
    .in0(B), .in1(not_1_out), .out(multiplexer_1_out), .sel(Binv));
  Comparator #(.width(32)) comparator_1 (.a(A), .b(B), .eq(Zero), .lt(comparator_1_lt));  // open: gt
  Adder #(.width(32)) adder_1 (.a(A), .b(multiplexer_1_out), .out(adder_1_out), .cin(Cin), .cout(Cout));
  assign bit_extender_1_out = {{31{1'b0}}, comparator_1_lt};  // Bit_Extender bit_extender_1
  Multiplexer #(.select(2), .width(32), .enable("false")) multiplexer_2 (
    .in0({32{1'b0}}), .in1(adder_1_out), .in2(bit_extender_1_out), .out(S), .sel(ALUop));  // open: in3
endmodule

module Control_Unit (
  input  [2:0] in_1,
  output [1:0] ALUop,
  output MemRead,
  output MemWrite,
  output Branch,
  output ALUsrc,
  output MemToReg,
  output RegDst,
  output WriteReg,
  output Binv,
  output Cin
);

  wire decoder_1_out2, decoder_1_out6;

  Decoder #(.select(3), .enable("false")) decoder_1 (
    .out1(Branch), .out2(decoder_1_out2), .out3(MemRead), .out4(Binv), .out5(ALUop[1]),
    .out6(decoder_1_out6), .out7(MemWrite), .sel(in_1));  // open: out0
  or or_1 (ALUop[0], Binv, MemRead, decoder_1_out2, decoder_1_out6, MemWrite, Branch);
  or or_2 (ALUsrc, decoder_1_out6, MemWrite, MemRead);
  or or_3 (WriteReg, MemRead, ALUop[1], decoder_1_out6, Binv, decoder_1_out2);
  or or_4 (RegDst, decoder_1_out6, MemRead);

  assign Cin = Binv;
  assign MemToReg = MemRead;
endmodule
